# Fritzing sketch 7_segment_parallel (saved by Fritzing 0.8.7b)
breadboards: 1

parts:
  7_Segment1 = 7 Segment Display
  Parte1 = Arduino Uno (Rev3)
  R1 = Resistor [tolerance=±5% resistance=220 package=THT]
  LED1 = LED - 5mm [color="Red (633nm)" package="5 mm [THT]"]
  R2 = Resistor [tolerance=±5% resistance=220 package=THT]

nets:
  N1: 7_Segment1.Segment_A#1, Parte1.D13/SCK
  N2: 7_Segment1.Segment_F, Parte1.D12/MISO
  N3: 7_Segment1.common_cathode#3, R1.Pin_0
  N4: 7_Segment1.Segment_E, Parte1.D11_PWM/MOSI
  N5: 7_Segment1.Segment_D, Parte1.D10_PWM/SS
  N6: 7_Segment1.Segment_DP, Parte1.D9_PWM
  N7: 7_Segment1.Segment_C, Parte1.D8
  N8: 7_Segment1.Segment_B, Parte1.D7
  N9: 7_Segment1.Segment_A#10, Parte1.D6_PWM
  N10: Parte1.D5_PWM, LED1.anode
  N11: Parte1.GND, R1.Pin_1, R2.Pin_1
  N12: LED1.cathode, R2.Pin_0
