# Fritzing sketch demo_photo_resistor_simplified (saved by Fritzing 0.8.7b)
breadboards: 1

parts:
  R1 = Resistor [tolerance=±5% resistance=10k package=THT]
  R2 = Photocell (LDR) [package=THT]
  Part1 = Arduino Uno (Rev3)
  R3 = Resistor [tolerance=±5% resistance=330 package=THT]
  R4 = Rotary Potentiometer (Small) [maximum_resistance=10kΩ package=THT]
  Q1 = NPN-Transistor [package="TO92 [THT]"]
  LED2 = RGB LED (com. cathode, rbg) [package="5 mm [THT]"]
  R8 = Resistor [tolerance=±5% resistance=220 package=THT]
  R11 = Resistor [tolerance=±5% resistance=10k package=THT]
  LED3 = LED - 5mm [color="White (8000K)" package="5 mm [THT]"]

nets (from the schematic view):
  N1: R1.Pin_0, R2.pin_1, Part1.A0
  N2: R1.Pin_1, Part1.GND, Q1.E
  N3: R2.pin_0, Part1.5V, R3.Pin_0
  N4: Part1.D8, R11.Pin_0
  N5: Part1.D4, LED2.red_anode
  N6: R3.Pin_1, LED3.anode
  N7: R4.wiper, LED3.cathode
  N8: Q1.B, R11.Pin_1
  N9: Q1.C, R8.Pin_1
  N10: LED2.common_cathode, R8.Pin_0
