# Fritzing sketch 74HC595_7SEGs - Double (saved by Fritzing 0.8.7b)
breadboards: 1

parts:
  Parte1 = Arduino Uno (Rev3)
  U1 = 74HC595 [package="DIP16 [THT]"]
  R1 = Resistor [tolerance=±5% resistance=220 package=THT]
  V1 = DC Power [voltage=5]  # not connected
  U2 = 7-SEGMENT-DISPLAY [package=7-segment-display]
  U3 = 74HC595 [package="DIP16 [THT]"]
  U4 = 7-SEGMENT-DISPLAY [package=7-segment-display]
  R2 = Resistor [tolerance=±5% resistance=220 package=THT]

nets (from the breadboard view):
  N1: Parte1.D8, U1.SH_CP, U3.SH_CP
  N2: Parte1.D9_PWM, U1.DS
  N3: Parte1.D10_PWM/SS, U1.MR, U3.MR
  N4: Parte1.D12/MISO, U1.ST_CP, U3.ST_CP
  VCC: Parte1.5V, U1.VCC, U3.OE, U3.VCC
  GND: Parte1.GND, U1.GND, U1.OE, R1.Pin_1, U3.GND, R2.Pin_1
  N5: U1.Q1, U2.A
  N6: U1.Q2, U2.DP
  N7: U1.Q3, U2.G1
  N8: U1.Q4, U2.D
  N9: U1.Q5, U2.E
  N10: U1.Q6, U2.G
  N11: U1.Q7, U2.B
  N12: U1.Q7', U3.DS
  N13: U1.Q0, U2.G2
  N14: R1.Pin_0, U2.C
  N15: U3.Q1, U4.A
  N16: U3.Q2, U4.DP
  N17: U3.Q3, U4.G1
  N18: U3.Q4, U4.D
  N19: U3.Q5, U4.G
  N20: U3.Q6, U4.E
  N21: U3.Q7, U4.B
  N22: U3.Q0, U4.G2
  N23: U4.C, R2.Pin_0
