# Fritzing sketch 74HC595_LEDs (saved by Fritzing 0.8.7b)
breadboards: 1

parts:
  SHIFT_REGISTER = 74HC595 [package="DIP16 [THT]"]
  INTEL_GALILEO = Arduino Uno (Rev3)
  LED3 = smd LED [color="Red (633nm)" package="0603 [SMD]"]
  LED4 = smd LED [color="Red (633nm)" package="0603 [SMD]"]
  LED5 = smd LED [color="Red (633nm)" package="0603 [SMD]"]
  LED6 = smd LED [color="Red (633nm)" package="0603 [SMD]"]
  LED7 = smd LED [color="Red (633nm)" package="0603 [SMD]"]
  LED8 = smd LED [color="Red (633nm)" package="0603 [SMD]"]
  LED9 = smd LED [color="Red (633nm)" package="0603 [SMD]"]
  R8 = Resistor [tolerance=±5% resistance=1k package=THT]
  LED2 = smd LED [color="Red (633nm)" package="0603 [SMD]"]

nets:
  N1: SHIFT_REGISTER.Q1, LED3.anode
  N2: SHIFT_REGISTER.Q2, LED4.anode
  N3: SHIFT_REGISTER.Q3, LED5.anode
  N4: SHIFT_REGISTER.Q4, LED6.anode
  N5: SHIFT_REGISTER.Q5, LED7.anode
  N6: SHIFT_REGISTER.Q6, LED8.anode
  N7: SHIFT_REGISTER.Q7, LED9.anode
  GND: SHIFT_REGISTER.GND, SHIFT_REGISTER.OE, INTEL_GALILEO.GND, R8.Pin_0
  N8: SHIFT_REGISTER.MR, INTEL_GALILEO.D10_PWM/SS
  N9: SHIFT_REGISTER.SH_CP, INTEL_GALILEO.D11_PWM/MOSI
  N10: SHIFT_REGISTER.ST_CP, INTEL_GALILEO.D12/MISO
  N11: SHIFT_REGISTER.DS, INTEL_GALILEO.D9_PWM
  N12: SHIFT_REGISTER.Q0, LED2.anode
  VCC: SHIFT_REGISTER.VCC, INTEL_GALILEO.5V
  N13: LED3.cathode, LED4.cathode, LED5.cathode, LED6.cathode, LED7.cathode, LED8.cathode, LED9.cathode, R8.Pin_1, LED2.cathode
