# Fritzing sketch semaforo (saved by Fritzing 0.8.7b)
circuit board: 8.46667cm x 5.64444cm
breadboards: 1

parts:
  Parte1 = Arduino Uno (Rev3)
  R1 = Resistor [tolerance=±5% resistance=470 package=THT]
  R2 = Resistor [tolerance=±5% resistance=470 package=THT]
  R3 = Resistor [tolerance=±5% resistance=470 package=THT]
  R4 = Resistor [tolerance=±5% resistance=470 package=THT]
  LED5 = LED - 5mm [color="White (6500K)" package="5 mm [THT]"]
  LED6 = LED - 5mm [color="Yellow (592nm)" package="5 mm [THT]"]
  LED7 = LED - 5mm [color="Red (633nm)" package="5 mm [THT]"]
  LED8 = LED - 5mm [color="Green (555nm)" package="5 mm [THT]"]
  V1 = DC Power [voltage=5]

nets:
  N1: Parte1.D10_PWM/SS, LED7.anode
  N2: Parte1.D11_PWM/MOSI, LED6.anode
  N3: Parte1.D12/MISO, R2.Pin_0, LED8.cathode, LED8.anode
  N4: Parte1.D13/SCK, R4.Pin_0, LED5.cathode, LED5.anode
  GND: Parte1.GND, R1.Pin_1, R2.Pin_1, R3.Pin_1, R4.Pin_1, V1.V-
  N5: Parte1.VIN, V1.V+
  N6: R1.Pin_0, LED7.cathode
  N7: R3.Pin_0, LED6.cathode
